# Fritzing sketch Esquema Laboratorio 1 (saved by Fritzing 0.9.5d)
breadboards: 1

parts:
  L298N1 = L298N DC motor driver
  M1 = DC Motor
  M2 = DC Motor
  Part1 = Arduino Uno (Rev3)
  HC-SR04_Sensor_1 = HC-SR04 Ultrasonic Distance Sensor
  VCC1 = Battery block 9V
  GY1 = MPU-6050 Board GY-521 [form="♀ (female)" package=THT]
  USBTTL1 = Micro USB B Plug
  USBTTL2 = USB A Plug
  D2 = Schottky Diode [part_number=1N5817 package="Melf DO-213 AB [SMD]"]  # not connected
  LCD1 = LCD screen
  LCM1602_IIC1 = LCM1602 IIC [part_number="LCM1602 IIC" chip_label="LCM1602 IIC" package="DIP (Dual Inline) [THT]"]

nets:
  N1: L298N1.OUT1, M2.pin_2
  N2: L298N1.OUT2, M2.pin_1
  N3: L298N1.OUT3, M1.pin_2
  N4: L298N1.OUT4, M1.pin_1
  N5: L298N1.12V, VCC1.+
  GND: L298N1.GND, Part1.GND, HC-SR04_Sensor_1.GND, VCC1.-, GY1.pin2
  5V: L298N1.5V#7, Part1.5V, HC-SR04_Sensor_1.VCC
  N6: L298N1.5V#9, L298N1.ENA
  N7: L298N1.5V#10, L298N1.ENB
  N8: L298N1.IN1, Part1.D8
  N9: L298N1.IN2, Part1.D7
  N10: L298N1.IN3, Part1.D5_PWM
  N11: L298N1.IN4, Part1.D4
  N12: Part1.A4/SDA, GY1.pin4
  N13: Part1.A5/SCL, GY1.pin3
  N14: Part1.D2, HC-SR04_Sensor_1.TRIG
  N15: Part1.D3_PWM, HC-SR04_Sensor_1.ECHO
  N16: Part1.3V3, GY1.pin1
  N17: USBTTL1.usb, USBTTL2.usb
  VSS: LCD1.VSS, LCM1602_IIC1.VSS
  VDD: LCD1.VDD, LCM1602_IIC1.VDD
  N18: LCD1.V0, LCM1602_IIC1.V0
  N19: LCD1.RS, LCM1602_IIC1.RS
  N20: LCD1.R/W, LCM1602_IIC1.RW
  N21: LCD1.E, LCM1602_IIC1.E
  N22: LCD1.DB0, LCM1602_IIC1.D0
  N23: LCD1.DB1, LCM1602_IIC1.D1
  N24: LCD1.DB2, LCM1602_IIC1.D2
  N25: LCD1.DB3, LCM1602_IIC1.D3
  N26: LCD1.DB4, LCM1602_IIC1.D4
  N27: LCD1.DB5, LCM1602_IIC1.D5
  N28: LCD1.DB6, LCM1602_IIC1.D6
  N29: LCD1.DB7, LCM1602_IIC1.D7
  N30: LCD1.LED+, LCM1602_IIC1.A
  N31: LCD1.LED-, LCM1602_IIC1.K
  N32: LCM1602_IIC1.LED_A, LCM1602_IIC1.LED_B

notes:
  Left Motor
  Right Motor
  L298N Motor Driver Board

custom parts:
  L298N DC motor driver: 2x DC motor driver with 78M05 positive voltage regulator (7..35 V) L298N: max 46 V, 2 A Set 5 V Enable jumper to enable 5 V regultor (needed for the L298N) and +5 V output at screw terminal or supply external +5 V at screw terminal Set ENA and/or ENB to +5 V to enable motor permanently or supply ENA and/or ENB with PWM signal IN1 and IN2 set rotation directory for motor A (OUT1/OUT2) IN2 and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
  MPU-6050 Board GY-521: Acelerometro y Giroscopio MPU-6050 Board GY-521
  LCM1602 IIC: I2C-Module to use a 1602 or 2004 LCD on with the wire.h libory Serial LCD Modul
