# Fritzing sketch Esquema Laboratorio 2 (saved by Fritzing 0.9.5d)
breadboards: 1

parts:
  L298N1 = L298N DC motor driver
  Part1 = Arduino Uno (Rev3)
  HC-SR04_Sensor_1 = HC-SR04 Ultrasonic Distance Sensor
  GY1 = MPU-6050 Board GY-521 [form="♀ (female)" package=THT]
  M3 = Getriebemotor
  M4 = Getriebemotor
  Part2 = Adafruit TCS34725 RGB Color Sensor [part_number="Adafruit #1334"]
  SERVO1 = Tower Pro SG90 servo [part_number=101246]
  VCC1 = Battery

nets:
  N1: L298N1.OUT1, M4.pin_2
  N2: L298N1.OUT2, M4.pin_1
  N3: L298N1.OUT3, M3.pin_2
  N4: L298N1.OUT4, M3.pin_1
  12V: L298N1.12V, Part1.VIN, VCC1.+
  GND: L298N1.GND, Part1.GND, HC-SR04_Sensor_1.GND, GY1.pin2, Part2.GND, SERVO1.GND, VCC1.-
  N5: L298N1.ENA, Part1.D9_PWM
  N6: L298N1.ENB, Part1.D10_PWM/SS
  N7: L298N1.IN1, Part1.D6_PWM
  N8: L298N1.IN2, Part1.D7
  N9: L298N1.IN3, Part1.D5_PWM
  N10: L298N1.IN4, Part1.D4
  N11: Part1.A2, GY1.pin4
  N12: Part1.A3, GY1.pin3
  N13: Part1.A4/SDA, Part2.SDA, Part2.INT
  N14: Part1.A5/SCL, Part2.SCL
  N15: Part1.D8, Part2.LED_EN
  N16: Part1.D11_PWM/MOSI, SERVO1.Signal
  N17: Part1.D2, HC-SR04_Sensor_1.TRIG
  N18: Part1.D3_PWM, HC-SR04_Sensor_1.ECHO
  5V: Part1.5V, HC-SR04_Sensor_1.VCC, GY1.pin1, Part2.VIN, SERVO1.+5V

notes:
  L298N Motor Driver Board
  Right Motor

custom parts:
  L298N DC motor driver: 2x DC motor driver with 78M05 positive voltage regulator (7..35 V) L298N: max 46 V, 2 A Set 5 V Enable jumper to enable 5 V regultor (needed for the L298N) and +5 V output at screw terminal or supply external +5 V at screw terminal Set ENA and/or ENB to +5 V to enable motor permanently or supply ENA and/or ENB with PWM signal IN1 and IN2 set rotation directory for motor A (OUT1/OUT2) IN2 and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
  MPU-6050 Board GY-521: Acelerometro y Giroscopio MPU-6050 Board GY-521
  Adafruit TCS34725 RGB Color Sensor: Your electronics can now see in dazzling color with this lovely color light sensor. We found the best color sensor on the market, the TCS34725, which has RGB and Clear light sensing elements. An IR blocking filter, integrated on-chip and localized to the color sensing photodiodes, minimizes the IR spectral component of the incoming light and allows color measurements to be made accurately. The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
  Tower Pro SG90 servo: Original file by John De Cristofaro http://www.adafruit.com/products/1449 Adafruit Feedback Servo (Small) Edited by: e-radionica.com 28/9/2015
  Battery: Your standard 2x 18650 battery pack (7,4 Volts)
